# Fritzing sketch schema (saved by Fritzing 0.9.3b)
breadboards: 1

parts:
  Part2 = Arduino Ethernet Shield (Rev3)
  LED1 = RGB LED (com. cathode, rgb) [package="5 mm [THT]"]
  LED2 = RGB LED (com. cathode, rgb) [package="5 mm [THT]"]
  S2 = Pushbutton [package="[THT]"]
  LED3 = RGB LED (com. cathode, rgb) [package="5 mm [THT]"]
  LED4 = RGB LED (com. cathode, rgb) [package="5 mm [THT]"]
  S3 = Pushbutton [package="[THT]"]
  S4 = Pushbutton [package="[THT]"]
  S5 = Pushbutton [package="[THT]"]
  Part1 = Arduino Mega 2560 (Rev3)

nets:
  N1: Part2.5V, LED1.green_anode, LED2.green_anode, S2.Pin_3, S2.Pin_4, LED3.green_anode, LED4.green_anode, S3.Pin_3, S3.Pin_4, S4.Pin_3, S4.Pin_4, S5.Pin_3, S5.Pin_4
  N2: Part2.GND, LED1.common_cathode, LED2.common_cathode, LED3.common_cathode, LED4.common_cathode
  N3: LED1.blue_anode, LED2.red_anode
  N4: LED2.blue_anode, LED4.red_anode
  N5: S2.Pin_1, S2.Pin_2
  N6: LED3.red_anode, LED4.blue_anode
  N7: LED3.blue_anode, Part1.D53
  N8: S3.Pin_1, S3.Pin_2
  N9: S4.Pin_1, S4.Pin_2
  N10: S5.Pin_1, S5.Pin_2
